# Fritzing sketch CEC_Interface (saved by Fritzing 0.9.2b)
stripboards: 1

parts:
  Part1 = Arduino Pro Mini v13
  Q2 = NPN-Transistor [package="TO92 [THT]"]
  Q1 = NPN-Transistor [package="TO92 [THT]"]
  D1 = Zener Diode [part_number=1N4732A breakdown_voltage=3.6V package="300 mil [THT]"]
  R2 = Resistor [tolerance=±5% resistance=330 package=THT]
  R5 = Resistor [tolerance=±5% resistance=27k package=THT]
  D2 = Rectifier Diode [part_number=1N4001 package="300 mil [THT]"]
  R10 = Resistor [tolerance=±5% resistance=100k package=THT]
  R11 = Resistor [tolerance=±5% resistance=1M package=THT]
  U1 = Header 1 [package=1x01_offset]
  U2 = Header 1 [package=1x01_offset]
  U3 = Header 1 [package=1x01_offset]
  R8 = Resistor [tolerance=±5% resistance=2k package=THT]
  R4 = Resistor [tolerance=±5% resistance=220 package=THT]
  R3 = Resistor [tolerance=±5% resistance=10k package=THT]

nets:
  5V: Part1.VCC, R2.Pin_1, R10.Pin_1, U2.1
  GND: Part1.GND, D1.anode, U3.1, R8.Pin_1, R4.Pin_1
  N1: Part1.D3_PWM, R3.Pin_1
  N2: Part1.D2, Q2.C, R10.Pin_0
  N3: Q2.E, R8.Pin_0
  N4: Q2.B, R11.Pin_1
  N5: Q1.E, R4.Pin_0
  N6: Q1.B, R3.Pin_0
  N7: Q1.C, D2.cathode, R11.Pin_0, U1.1
  3.3 V: D1.cathode, R2.Pin_0, R5.Pin_1
  N8: R5.Pin_0, D2.anode

notes:
  GND (17)
  VCC (18)
  CEC (13)
